# Fritzing sketch Breadboard (saved by Fritzing 0.9.3b)
breadboards: 1

parts:
  Part1 = Arduino Micro (Rev3)
  Part2 = NRF24L01+ Breakout Board
  Part3 = LCD1602-I2C

nets:
  N1: Part1.MOSI, Part2.MOSI
  GND: Part1.GND, Part2.GND, Part3.GND
  sda: Part1.D2/SDA, Part3.SDA
  scl: Part1.D3/SCL, Part3.SCL
  N2: Part1.D4_PWM/A6, Part2.CE
  N3: Part1.D5_PWM, Part2.CS
  N4: Part1.SCK, Part2.SCK
  N5: Part1.MISO, Part2.MISO
  5V: Part1.5V, Part3.VCC
  3V3: Part1.3V3, Part2.VCC

custom parts:
  LCD1602-I2C: A standard character display, usually with 2x16 characters. Comes in many colors with LCM1602 IIC attached.
